// Logisim project P3.circ as structural Verilog: 9 circuits, main circuit main
module main (
  input  Reset,
  output [31:0] out_2,
  output out_3,
  output [4:0] out_4,
  output [31:0] out_5,
  output out_6,
  output [4:0] out_7,
  output [31:0] out_8
);

  wire alu_1_zero, and_1_out, and_logic_1_add, and_logic_1_beq, and_logic_1_lui, and_logic_1_lw,
       and_logic_1_ori, and_logic_1_sub, and_logic_1_sw, clk, or_logic_1_alusrc, or_logic_1_branch,
       or_logic_1_mem2reg, or_logic_1_regdest;
  wire [2:0] or_logic_1_aluctrl;
  wire [7:0] adder_1_out, ifu_1_pcnxt;
  wire [31:0] bit_extender_1_out, dm_1_rd, grf_1_rd1, MemAddr, multiplexer_2_out, shifter_1_out;

  IFU ifu_1 (.PCSrc(and_1_out), .PCBranch(adder_1_out), .Inst(out_2), .Reset(Reset), .clk(clk), .PCNxt(ifu_1_pcnxt));
  Clock u_clk (.out(clk));
  AND_logic and_logic_1 (
    .func(out_2[5:0]), .op(out_2[31:26]), .add(and_logic_1_add), .sub(and_logic_1_sub),
    .ori(and_logic_1_ori), .lw(and_logic_1_lw), .sw(and_logic_1_sw), .beq(and_logic_1_beq),
    .lui(and_logic_1_lui));
  // Probe on out_2[31:26]
  // Probe on out_2[25:21]
  // Probe on out_2[20:16]
  OR_logic or_logic_1 (
    .add(and_logic_1_add), .sub(and_logic_1_sub), .ori(and_logic_1_ori), .lw(and_logic_1_lw),
    .sw(and_logic_1_sw), .beq(and_logic_1_beq), .lui(and_logic_1_lui), .Mem2Reg(or_logic_1_mem2reg),
    .MemWrite(out_6), .Branch(or_logic_1_branch), .ALUCtrl(or_logic_1_aluctrl), .ALUSrc(or_logic_1_alusrc),
    .RegDest(or_logic_1_regdest), .RegWrite(out_3));
  // Probe on out_2[5:0]
  // Probe on out_2[15:11]
  // Probe on out_4
  assign bit_extender_1_out = {{16{out_2[15]}}, out_2[15:0]};  // Bit_Extender bit_extender_1
  // Probe on out_5
  GRF grf_1 (
    .reset(Reset), .WE(out_3), .WD(out_5), .clk(clk), .A3(out_4), .A1(out_2[25:21]), .A2(out_2[20:16]),
    .RD1(grf_1_rd1), .RD2(out_8));
  // Probe on bit_extender_1_out
  // Probe on ifu_1_pcnxt
  // Probe on grf_1_rd1
  // Probe on out_8
  Multiplexer #(.width(5), .disabled(0), .enable("false")) multiplexer_1 (
    .in0(out_2[20:16]), .in1(out_2[15:11]), .out(out_4), .sel(or_logic_1_regdest));
  // Probe on multiplexer_2_out
  Multiplexer #(.width(32), .disabled(0), .enable("false")) multiplexer_2 (
    .in0(out_8), .in1(bit_extender_1_out), .out(multiplexer_2_out), .sel(or_logic_1_alusrc));
  // Probe on out_8
  // Probe on bit_extender_1_out
  // Probe on shifter_1_out[7:0]
  Shifter #(.width(32)) shifter_1 (.in(bit_extender_1_out), .\dist (5'b00010), .out(shifter_1_out));
  // Probe on adder_1_out
  and and_1 (and_1_out, or_logic_1_branch, alu_1_zero);
  ALU alu_1 (
    .SrcA(grf_1_rd1), .SrcB(multiplexer_2_out), .Zero(alu_1_zero),
    .ALUResult({MemAddr[31:7], out_7, MemAddr[1:0]}), .ALUCtrl(or_logic_1_aluctrl));
  // Probe on {MemAddr[31:7], out_7, MemAddr[1:0]}
  Adder adder_1 (.a(shifter_1_out[7:0]), .b(ifu_1_pcnxt), .out(adder_1_out));  // open: cin, cout
  DM dm_1 (.Addr({MemAddr[31:7], out_7, MemAddr[1:0]}), .WD(out_8), .RD(dm_1_rd), .Reset(Reset), .WE(out_6), .clk(clk));
  Multiplexer #(.width(32), .disabled(0), .enable("false")) multiplexer_3 (
    .in0({MemAddr[31:7], out_7, MemAddr[1:0]}), .in1(dm_1_rd), .out(out_5), .sel(or_logic_1_mem2reg));
  // Probe on dm_1_rd
  // Probe on out_5

  // Other names for the same wires on the sheet: Instr[31:0] = out_2; MemData[31:0] = out_8; MemWrite = out_6;
  //   MemAddr[6:2] = out_7; RegAddr[4:0] = out_4; RegData[31:0] = out_5; RegWrite = out_3
endmodule

module AND_logic (
  input  [5:0] func,
  input  [5:0] op,
  output add,
  output sub,
  output ori,
  output lw,
  output sw,
  output beq,
  output lui
);

  and and_1 (add, func[5], ~func[4], ~func[3], ~func[2], ~func[1], ~func[0], ~op[5], ~op[4], ~op[3], ~op[2], ~op[1], ~op[0]);  // AND_Gate
  and and_2 (sub, func[5], ~func[4], ~func[3], ~func[2], func[1], ~func[0], ~op[5], ~op[4], ~op[3], ~op[2], ~op[1], ~op[0]);  // AND_Gate
  and and_3 (ori, ~op[5], ~op[4], op[3], op[2], ~op[1], op[0]);  // AND_Gate
  and and_4 (lw, op[5], ~op[4], ~op[3], ~op[2], op[1], op[0]);  // AND_Gate
  and and_5 (sw, op[5], ~op[4], op[3], ~op[2], op[1], op[0]);  // AND_Gate
  and and_6 (beq, ~op[5], ~op[4], ~op[3], op[2], ~op[1], ~op[0]);  // AND_Gate
  and and_7 (lui, ~op[5], ~op[4], op[3], op[2], op[1], op[0]);  // AND_Gate
endmodule

module ALU (
  input  [31:0] SrcA,
  input  [2:0] ALUCtrl,
  input  [31:0] SrcB,
  output Zero,
  output [31:0] ALUResult
);

  wire [31:0] adder_1_out, and_1_out, or_1_out, or_2_out, subtractor_1_out;

  assign or_1_out = SrcA | SrcB;  // OR_Gate or_1, 32 bits wide
  assign and_1_out = SrcA & SrcB;  // AND_Gate and_1, 32 bits wide
  Adder #(.width(32)) adder_1 (.a(SrcA), .b(SrcB), .out(adder_1_out));  // open: cin, cout
  Subtractor #(.width(32)) subtractor_1 (.a(SrcA), .b(SrcB), .out(subtractor_1_out));  // open: bin, bout
  assign or_2_out = SrcA | {{16{1'b0}}, SrcB[15:0]};  // OR_Gate or_2, 32 bits wide
  Multiplexer #(.select(3), .width(32), .disabled(0), .enable("false")) multiplexer_1 (
    .in0(or_1_out), .in1(and_1_out), .in2(adder_1_out), .in3(subtractor_1_out),
    .in4({SrcB[15:0], {16{1'b0}}}), .in5(or_2_out), .out(ALUResult), .sel(ALUCtrl));  // open: in6, in7
  Comparator #(.width(32), .mode("unsigned")) comparator_1 (.a({32{1'b0}}), .b(ALUResult), .eq(Zero));  // open: gt, lt
endmodule

module GRF (
  input  reset,
  input  WE,
  input  [31:0] WD,
  input  clk,
  input  [4:0] A3,
  input  [4:0] A1,
  input  [4:0] A2,
  output [31:0] RD1,
  output [31:0] RD2
);

  wire W00, W01, W02, W03, W04, W05, W06, W07, W10, W11, W12, W13, W14, W15, W16, W17, W20, W21, W22, W23,
       W24, W25, W26, W27, W30, W31, W32, W33, W34, W35, W36, W37;
  wire [31:0] multiplexer_1_out, multiplexer_2_out, multiplexer_3_out, multiplexer_4_out, multiplexer_5_out,
       multiplexer_6_out, multiplexer_7_out, multiplexer_9_out, register_1_q, register_2_q, register_3_q,
       register_4_q, register_5_q, register_6_q, register_7_q, register_8_q, register_9_q, register_10_q,
       register_11_q, register_12_q, register_13_q, register_14_q, register_15_q, register_16_q,
       register_17_q, register_18_q, register_19_q, register_20_q, register_21_q, register_22_q,
       register_23_q, register_24_q, register_25_q, register_26_q, register_27_q, register_28_q,
       register_29_q, register_30_q, register_31_q, register_32_q;

  Register #(.width(32)) register_1 (.D(WD), .en(W30), .Q(register_1_q), .clk(clk), .clr(reset));
  Register #(.width(32)) register_2 (.D(WD), .en(W31), .Q(register_2_q), .clk(clk), .clr(reset));
  Register #(.width(32)) register_3 (.D(WD), .en(W32), .Q(register_3_q), .clk(clk), .clr(reset));
  Register #(.width(32)) register_4 (.D(WD), .en(W33), .Q(register_4_q), .clk(clk), .clr(reset));
  Register #(.width(32)) register_5 (.D(WD), .en(W34), .Q(register_5_q), .clk(clk), .clr(reset));
  Register #(.width(32)) register_6 (.D(WD), .en(W35), .Q(register_6_q), .clk(clk), .clr(reset));
  Register #(.width(32)) register_7 (.D(WD), .en(W36), .Q(register_7_q), .clk(clk), .clr(reset));
  Register #(.width(32)) register_8 (.D(WD), .en(W37), .Q(register_8_q), .clk(clk), .clr(reset));
  Register #(.width(32)) register_9 (.D(WD), .en(W20), .Q(register_9_q), .clk(clk), .clr(reset));
  Register #(.width(32)) register_10 (.D(WD), .en(W21), .Q(register_10_q), .clk(clk), .clr(reset));
  Register #(.width(32)) register_11 (.D(WD), .en(W22), .Q(register_11_q), .clk(clk), .clr(reset));
  Register #(.width(32)) register_12 (.D(WD), .en(W23), .Q(register_12_q), .clk(clk), .clr(reset));
  Register #(.width(32)) register_13 (.D(WD), .en(W24), .Q(register_13_q), .clk(clk), .clr(reset));
  Register #(.width(32)) register_14 (.D(WD), .en(W25), .Q(register_14_q), .clk(clk), .clr(reset));
  Register #(.width(32)) register_15 (.D(WD), .en(W26), .Q(register_15_q), .clk(clk), .clr(reset));
  Register #(.width(32)) register_16 (.D(WD), .en(W27), .Q(register_16_q), .clk(clk), .clr(reset));
  Multiplexer #(.select(3), .width(32), .enable("false")) multiplexer_1 (
    .in0(register_1_q), .in1(register_2_q), .in2(register_3_q), .in3(register_4_q), .in4(register_5_q),
    .in5(register_6_q), .in6(register_7_q), .in7(register_8_q), .out(multiplexer_1_out), .sel(A1[2:0]));
  Multiplexer #(.select(3), .width(32), .enable("false")) multiplexer_2 (
    .in0(register_1_q), .in1(register_2_q), .in2(register_3_q), .in3(register_4_q), .in4(register_5_q),
    .in5(register_6_q), .in6(register_7_q), .in7(register_8_q), .out(multiplexer_2_out), .sel(A2[2:0]));
  Multiplexer #(.select(3), .width(32), .enable("false")) multiplexer_3 (
    .in0(register_9_q), .in1(register_10_q), .in2(register_11_q), .in3(register_12_q), .in4(register_13_q),
    .in5(register_14_q), .in6(register_15_q), .in7(register_16_q), .out(multiplexer_3_out), .sel(A1[2:0]));
  Multiplexer #(.select(3), .width(32), .enable("false")) multiplexer_4 (
    .in0(register_9_q), .in1(register_10_q), .in2(register_11_q), .in3(register_12_q), .in4(register_13_q),
    .in5(register_14_q), .in6(register_15_q), .in7(register_16_q), .out(multiplexer_4_out), .sel(A2[2:0]));
  Register #(.width(32)) register_17 (.D(WD), .en(W10), .Q(register_17_q), .clk(clk), .clr(reset));
  Register #(.width(32)) register_18 (.D(WD), .en(W11), .Q(register_18_q), .clk(clk), .clr(reset));
  Register #(.width(32)) register_19 (.D(WD), .en(W12), .Q(register_19_q), .clk(clk), .clr(reset));
  Register #(.width(32)) register_20 (.D(WD), .en(W13), .Q(register_20_q), .clk(clk), .clr(reset));
  Register #(.width(32)) register_21 (.D(WD), .en(W14), .Q(register_21_q), .clk(clk), .clr(reset));
  Register #(.width(32)) register_22 (.D(WD), .en(W15), .Q(register_22_q), .clk(clk), .clr(reset));
  Register #(.width(32)) register_23 (.D(WD), .en(W16), .Q(register_23_q), .clk(clk), .clr(reset));
  Register #(.width(32)) register_24 (.D(WD), .en(W17), .Q(register_24_q), .clk(clk), .clr(reset));
  Multiplexer #(.select(3), .width(32), .enable("false")) multiplexer_5 (
    .in0(register_17_q), .in1(register_18_q), .in2(register_19_q), .in3(register_20_q), .in4(register_21_q),
    .in5(register_22_q), .in6(register_23_q), .in7(register_24_q), .out(multiplexer_5_out), .sel(A1[2:0]));
  Multiplexer #(.select(3), .width(32), .enable("false")) multiplexer_6 (
    .in0(register_17_q), .in1(register_18_q), .in2(register_19_q), .in3(register_20_q), .in4(register_21_q),
    .in5(register_22_q), .in6(register_23_q), .in7(register_24_q), .out(multiplexer_6_out), .sel(A2[2:0]));
  Register #(.width(32)) register_25 (.Q(register_25_q), .clk(W00), .clr(1'b1));  // open: D, en
  Register #(.width(32)) register_26 (.D(WD), .en(W01), .Q(register_26_q), .clk(clk), .clr(reset));
  Register #(.width(32)) register_27 (.D(WD), .en(W02), .Q(register_27_q), .clk(clk), .clr(reset));
  Register #(.width(32)) register_28 (.D(WD), .en(W03), .Q(register_28_q), .clk(clk), .clr(reset));
  Register #(.width(32)) register_29 (.D(WD), .en(W04), .Q(register_29_q), .clk(clk), .clr(reset));
  Register #(.width(32)) register_30 (.D(WD), .en(W05), .Q(register_30_q), .clk(clk), .clr(reset));
  Register #(.width(32)) register_31 (.D(WD), .en(W06), .Q(register_31_q), .clk(clk), .clr(reset));
  Register #(.width(32)) register_32 (.D(WD), .en(W07), .Q(register_32_q), .clk(clk), .clr(reset));
  Demultiplexer #(.select(5), .disabled(0), .enable("false")) demultiplexer_1 (
    .out0(W00), .out1(W01), .out2(W02), .out3(W03), .out4(W04), .out5(W05), .out6(W06), .out7(W07),
    .out8(W10), .out9(W11), .out10(W12), .out11(W13), .out12(W14), .out13(W15), .out14(W16), .out15(W17),
    .out16(W20), .out17(W21), .out18(W22), .out19(W23), .out20(W24), .out21(W25), .out22(W26), .out23(W27),
    .out24(W30), .out25(W31), .out26(W32), .out27(W33), .out28(W34), .out29(W35), .out30(W36), .out31(W37),
    .in(WE), .sel(A3));
  Multiplexer #(.select(3), .width(32), .enable("false")) multiplexer_7 (
    .in0(register_25_q), .in1(register_26_q), .in2(register_27_q), .in3(register_28_q), .in4(register_29_q),
    .in5(register_30_q), .in6(register_31_q), .in7(register_32_q), .out(multiplexer_7_out), .sel(A1[2:0]));
  Multiplexer #(.select(2), .width(32), .enable("false")) multiplexer_8 (
    .in0(multiplexer_7_out), .in1(multiplexer_5_out), .in2(multiplexer_3_out), .in3(multiplexer_1_out),
    .out(RD1), .sel(A1[4:3]));
  Multiplexer #(.select(3), .width(32), .enable("false")) multiplexer_9 (
    .in0(register_25_q), .in1(register_26_q), .in2(register_27_q), .in3(register_28_q), .in4(register_29_q),
    .in5(register_30_q), .in6(register_31_q), .in7(register_32_q), .out(multiplexer_9_out), .sel(A2[2:0]));
  Multiplexer #(.select(2), .width(32), .enable("false")) multiplexer_10 (
    .in0(multiplexer_9_out), .in1(multiplexer_6_out), .in2(multiplexer_4_out), .in3(multiplexer_2_out),
    .out(RD2), .sel(A2[4:3]));

  // Other names for the same wires on the sheet: A1sel[1:0] = A1[4:3]; A2sel[1:0] = A2[4:3]
endmodule

module DM (
  input  [31:0] Addr,
  input  [31:0] WD,
  input  WE,
  input  Reset,
  input  clk,
  output [31:0] RD
);

  wire not_1_out;

  RAM #(.addrWidth(5), .dataWidth(32), .bus("separate")) ram_1 (
    .addr(Addr[6:2]), .din(WD), .data(RD), .str(WE), .clk(clk), .ld(not_1_out), .clr(Reset));  // open: sel
  not not_1 (not_1_out, WE);
endmodule

module IFU (
  input  Reset,
  input  PCSrc,
  input  [7:0] PCBranch,
  input  clk,
  output [31:0] Inst,
  output [7:0] PCNxt
);

  wire [7:0] multiplexer_1_out, PC_q;

  Multiplexer #(.width(8), .disabled(0), .enable("false")) multiplexer_1 (
    .in0(PCNxt), .in1(PCBranch), .out(multiplexer_1_out), .sel(PCSrc));
  Register PC (.D(multiplexer_1_out), .Q(PC_q), .clk(clk), .clr(Reset));  // open: en
  Adder adder_1 (.a(PC_q), .b(8'h4), .out(PCNxt));  // open: cin, cout
  ROM #(.addrWidth(5), .dataWidth(32)) rom_1 (.addr(PC_q[6:2]), .data(Inst));  // open: sel

  // Notes on the sheet:
  //   contents of rom_1 (hex, n*v repeats v):
  //   3404007b 348501c8 3c06007b 3c07ffff 34e7ffff 868020 878820 e79020 34080000 ad040000 ad050004
  //   ad060008 ad07000c ad100010 ad110014 ad120018 8d040000 8d05000c ad04001c ad050020 34040001 34050002
  //   34060001 10850001 10860001 ad040024 ad050028
endmodule

module OR_logic (
  input  add,
  input  sub,
  input  ori,
  input  lw,
  input  sw,
  input  beq,
  input  lui,
  output Mem2Reg,
  output MemWrite,
  output Branch,
  output [2:0] ALUCtrl,
  output ALUSrc,
  output RegDest,
  output RegWrite
);

  wire add_out, and_out, lui_out, or_2_out, or_3_out, or_out, ori_out, sub_out;

  buf \or  (or_out, 1'b0);  // OR_Gate
  buf \and  (and_out, 1'b0);  // OR_Gate
  or u_add (add_out, sw, lw, add);
  or u_sub (sub_out, sub, beq);
  buf u_lui (lui_out, lui);  // OR_Gate
  or u_ori (ori_out, ori, 1'b0);
  buf or_2 (or_2_out, 1'b0);  // OR_Gate
  buf or_3 (or_3_out, 1'b0);  // OR_Gate
  or or_4 (ALUSrc, lui, sw, lw, ori);
  or or_5 (RegDest, sub, add);
  or or_6 (RegWrite, lui, lw, ori, sub, add);
  Translate translate_1 (
    .in0(or_out), .in1(and_out), .in2(add_out), .in3(sub_out), .in4(lui_out), .in5(ori_out), .in6(or_2_out),
    .in7(or_3_out), .out0(ALUCtrl[0]), .out1(ALUCtrl[1]), .out2(ALUCtrl[2]));

  assign Branch = beq;
  assign Mem2Reg = lw;
  assign MemWrite = sw;
endmodule

module Translate (
  input  in0,
  input  in1,
  input  in2,
  input  in3,
  input  in4,
  input  in5,
  input  in6,
  input  in7,
  output out0,
  output out1,
  output out2
);

  wire and_1_out, and_2_out, and_3_out, and_4_out, and_5_out, and_6_out, and_7_out, and_8_out, and_9_out,
       and_10_out, and_11_out, and_12_out, not_1_out, not_2_out, not_3_out, not_4_out, not_5_out, not_6_out,
       not_7_out, not_8_out, not_9_out, not_10_out, not_11_out, not_12_out, not_13_out, not_14_out,
       not_15_out, not_16_out, not_17_out, not_18_out, not_19_out, not_20_out, not_21_out, not_22_out,
       not_23_out, not_24_out, not_25_out, not_26_out, not_27_out, not_28_out, not_29_out, not_30_out,
       not_31_out, not_32_out, not_33_out, not_34_out, not_35_out, not_36_out, not_37_out, not_38_out,
       not_39_out, not_40_out, not_41_out, not_42_out, not_43_out, not_44_out, not_45_out, not_46_out,
       not_47_out, not_48_out, not_49_out, not_50_out, not_51_out, not_52_out, not_53_out, not_54_out,
       not_55_out, not_56_out, not_57_out, not_58_out, not_59_out, not_60_out, not_61_out, not_62_out,
       not_63_out, not_64_out, not_65_out, not_66_out, not_67_out, not_68_out, not_69_out, not_70_out,
       not_71_out, not_72_out, not_73_out, not_74_out, not_75_out, not_76_out, not_77_out, not_78_out,
       not_79_out, not_80_out, not_81_out, not_82_out, not_83_out, not_84_out;

  not not_1 (not_1_out, in0);
  not not_2 (not_2_out, in1);
  not not_3 (not_3_out, in2);
  not not_4 (not_4_out, in3);
  not not_5 (not_5_out, in4);
  not not_6 (not_6_out, in5);
  not not_7 (not_7_out, in6);
  not not_8 (not_8_out, in0);
  not not_9 (not_9_out, in1);
  not not_10 (not_10_out, in2);
  not not_11 (not_11_out, in3);
  not not_12 (not_12_out, in4);
  not not_13 (not_13_out, in6);
  not not_14 (not_14_out, in7);
  not not_15 (not_15_out, in0);
  not not_16 (not_16_out, in1);
  not not_17 (not_17_out, in2);
  not not_18 (not_18_out, in4);
  not not_19 (not_19_out, in5);
  not not_20 (not_20_out, in6);
  not not_21 (not_21_out, in7);
  not not_22 (not_22_out, in0);
  not not_23 (not_23_out, in2);
  not not_24 (not_24_out, in3);
  not not_25 (not_25_out, in4);
  not not_26 (not_26_out, in5);
  not not_27 (not_27_out, in6);
  not not_28 (not_28_out, in7);
  not not_29 (not_29_out, in0);
  not not_30 (not_30_out, in1);
  not not_31 (not_31_out, in2);
  not not_32 (not_32_out, in3);
  not not_33 (not_33_out, in4);
  not not_34 (not_34_out, in5);
  not not_35 (not_35_out, in6);
  not not_36 (not_36_out, in0);
  not not_37 (not_37_out, in1);
  not not_38 (not_38_out, in2);
  not not_39 (not_39_out, in3);
  not not_40 (not_40_out, in4);
  not not_41 (not_41_out, in5);
  not not_42 (not_42_out, in7);
  not not_43 (not_43_out, in0);
  not not_44 (not_44_out, in1);
  not not_45 (not_45_out, in2);
  not not_46 (not_46_out, in4);
  not not_47 (not_47_out, in5);
  not not_48 (not_48_out, in6);
  not not_49 (not_49_out, in7);
  not not_50 (not_50_out, in0);
  not not_51 (not_51_out, in1);
  not not_52 (not_52_out, in3);
  not not_53 (not_53_out, in4);
  not not_54 (not_54_out, in5);
  not not_55 (not_55_out, in6);
  not not_56 (not_56_out, in7);
  not not_57 (not_57_out, in0);
  not not_58 (not_58_out, in1);
  not not_59 (not_59_out, in2);
  not not_60 (not_60_out, in3);
  not not_61 (not_61_out, in4);
  not not_62 (not_62_out, in5);
  not not_63 (not_63_out, in6);
  not not_64 (not_64_out, in0);
  not not_65 (not_65_out, in1);
  not not_66 (not_66_out, in2);
  not not_67 (not_67_out, in3);
  not not_68 (not_68_out, in4);
  not not_69 (not_69_out, in5);
  not not_70 (not_70_out, in7);
  not not_71 (not_71_out, in0);
  not not_72 (not_72_out, in1);
  not not_73 (not_73_out, in2);
  not not_74 (not_74_out, in3);
  not not_75 (not_75_out, in4);
  not not_76 (not_76_out, in6);
  not not_77 (not_77_out, in7);
  not not_78 (not_78_out, in0);
  not not_79 (not_79_out, in1);
  not not_80 (not_80_out, in2);
  not not_81 (not_81_out, in3);
  not not_82 (not_82_out, in5);
  not not_83 (not_83_out, in6);
  not not_84 (not_84_out, in7);
  and and_1 (and_1_out, not_1_out, not_2_out, not_3_out, not_4_out, not_5_out, not_6_out, not_7_out, in7);
  and and_2 (and_2_out, not_8_out, not_9_out, not_10_out, not_11_out, not_12_out, in5, not_13_out, not_14_out);
  and and_3 (and_3_out, not_15_out, not_16_out, not_17_out, in3, not_18_out, not_19_out, not_20_out, not_21_out);
  and and_4 (and_4_out, not_22_out, in1, not_23_out, not_24_out, not_25_out, not_26_out, not_27_out, not_28_out);
  and and_5 (and_5_out, not_29_out, not_30_out, not_31_out, not_32_out, not_33_out, not_34_out, not_35_out, in7);
  and and_6 (and_6_out, not_36_out, not_37_out, not_38_out, not_39_out, not_40_out, not_41_out, in6, not_42_out);
  and and_7 (and_7_out, not_43_out, not_44_out, not_45_out, in3, not_46_out, not_47_out, not_48_out, not_49_out);
  and and_8 (and_8_out, not_50_out, not_51_out, in2, not_52_out, not_53_out, not_54_out, not_55_out, not_56_out);
  and and_9 (and_9_out, not_57_out, not_58_out, not_59_out, not_60_out, not_61_out, not_62_out, not_63_out, in7);
  and and_10 (and_10_out, not_64_out, not_65_out, not_66_out, not_67_out, not_68_out, not_69_out, in6, not_70_out);
  and and_11 (and_11_out, not_71_out, not_72_out, not_73_out, not_74_out, not_75_out, in5, not_76_out, not_77_out);
  and and_12 (and_12_out, not_78_out, not_79_out, not_80_out, not_81_out, in4, not_82_out, not_83_out, not_84_out);
  or or_1 (out0, and_1_out, and_2_out, and_3_out, and_4_out);
  or or_2 (out1, and_5_out, and_6_out, and_7_out, and_8_out);
  or or_3 (out2, and_9_out, and_10_out, and_11_out, and_12_out);
endmodule

module tb (
  input  in_1
);

  wire clock_1_out, clock_2_out, clock_3_out, clock_4_out, comparator_1_eq, comparator_2_eq, comparator_3_eq,
       main_1_out_3;
  wire [4:0] main_1_out_4;
  wire [7:0] counter_1_q;
  wire [31:0] bit_extender_1_out, main_1_out_2, main_1_out_5, or_1_out, rom_1_data, rom_2_data, rom_3_data;

  Counter counter_1 (.Q(counter_1_q), .clk(clock_1_out), .clr(in_1));  // open: load, D, count, carry
  Clock clock_1 (.out(clock_1_out));
  main main_1 (
    .Reset(in_1), .out_2(main_1_out_2), .out_3(main_1_out_3), .out_4(main_1_out_4), .out_5(main_1_out_5));  // open: out_6, out_7, out_8
  // Probe on main_1_out_4
  // Probe on main_1_out_5
  ROM #(.dataWidth(32)) rom_1 (.addr(counter_1_q), .data(rom_1_data));  // open: sel
  ROM #(.dataWidth(32)) rom_2 (.addr(counter_1_q), .data(rom_2_data));  // open: sel
  ROM #(.dataWidth(32)) rom_3 (.addr(counter_1_q), .data(rom_3_data));  // open: sel
  Comparator #(.width(32), .mode("unsigned")) comparator_1 (
    .a(rom_1_data), .b(main_1_out_2), .eq(comparator_1_eq));  // open: gt, lt
  Comparator #(.width(32), .mode("unsigned")) comparator_2 (
    .a(rom_2_data), .b(bit_extender_1_out), .eq(comparator_2_eq));  // open: gt, lt
  assign or_1_out = rom_2_data | rom_3_data;  // OR_Gate or_1, 32 bits wide
  Comparator #(.width(32), .mode("unsigned")) comparator_3 (
    .a(rom_3_data), .b(main_1_out_5), .eq(comparator_3_eq));  // open: gt, lt
  // Probe on bit_extender_1_out
  Comparator #(.width(32), .mode("unsigned")) comparator_4 (.a(or_1_out), .b({32{1'b0}}));  // open: gt, eq, lt
  assign bit_extender_1_out = {{27{1'b0}}, main_1_out_4};  // Bit_Extender bit_extender_1
  Clock clock_2 (.out(clock_2_out));
  Clock clock_3 (.out(clock_3_out));
  Clock clock_4 (.out(clock_4_out));
  Counter #(.trigger("falling")) counter_2 (
    .count(comparator_1_eq), .clk(clock_2_out), .clr(in_1));  // open: load, D, Q, carry
  Counter #(.trigger("falling")) counter_3 (
    .count(comparator_2_eq), .clk(clock_3_out), .clr(in_1));  // open: load, D, Q, carry
  Counter #(.trigger("falling")) counter_4 (
    .count(comparator_3_eq), .clk(clock_4_out), .clr(in_1));  // open: load, D, Q, carry

  // Notes on the sheet:
  //   contents of rom_1 (hex, n*v repeats v):
  //   3404007b 348501c8 3c06007b 3c07ffff 34e7ffff 868020 878820 e79020 34080000 ad040000 ad050004
  //   ad060008 ad07000c ad100010 ad110014 ad120018 8d040000 8d05000c ad04001c ad050020 34040001 34050002
  //   34060001 10850001 10860001 ad040024 ad050028
  //   contents of rom_2 (hex, n*v repeats v):
  //   4 5 6 7 7 10 11 12 9*0 5 0 0 4 5 6
  //   contents of rom_3 (hex, n*v repeats v):
  //   7b 1fb 7b0000 ffff0000 ffffffff 7b007b 7a fffffffe 9*0 ffffffff 0 0 1 2 1
endmodule
